# Fritzing sketch aciduino_lite_v2-teensy (saved by Fritzing 0.9.3b)
breadboards: 1

parts:
  S2 = Momentary Switch [package=ksa_sealed_tac_switch]
  S4 = Momentary Switch [package=ksa_sealed_tac_switch]
  S1 = Momentary Switch [package=ksa_sealed_tac_switch]
  S3 = Momentary Switch [package=ksa_sealed_tac_switch]
  S7 = Momentary Switch [package=ksa_sealed_tac_switch]
  S5 = Momentary Switch [package=ksa_sealed_tac_switch]
  S6 = Momentary Switch [package=ksa_sealed_tac_switch]
  S8 = Momentary Switch [package=ksa_sealed_tac_switch]
  R1 = Rotary Potentiometer (Small) [maximum_resistance=100kΩ package=THT]
  S9 = Momentary Switch [package=ksa_sealed_tac_switch]
  OLED1 = OLED 128x64 I2C Monochrome Display VDD-GND
  Teensy_LC1 = Teensy-LC
  S10 = Momentary Switch [package=ksa_sealed_tac_switch]

nets:
  N1: S2.2, Teensy_LC1.A1/D15
  N2: S2.4, S4.1, S4.2, S7.3, S7.4, S8.1, S8.2, S9.3, S9.4, Teensy_LC1.GND, Teensy_LC1.D2, Teensy_LC1.D8, S10.3, S10.4
  N3: S4.3, S4.4, Teensy_LC1.D9
  N4: S1.1, S3.3, S3.4, S5.3, S5.4, S6.1, S6.2, R1.leg2, OLED1.GND, Teensy_LC1.A8/D22, Teensy_LC1.AGND, Teensy_LC1.A10, Teensy_LC1.VUSB
  N5: S1.3, Teensy_LC1.A2/D16
  N6: S3.1, S3.2, Teensy_LC1.A3/D17
  N7: S7.1, S7.2, Teensy_LC1.D3
  N8: S5.1, S5.2, Teensy_LC1.D6
  N9: S6.3, S6.4, Teensy_LC1.D7
  N10: S8.3, S8.4, Teensy_LC1.D5
  VDD: R1.leg1, OLED1.VDD, Teensy_LC1.3V3
  N11: R1.wiper, Teensy_LC1.A9/D23, Teensy_LC1.AREF
  N12: S9.1, S9.2, Teensy_LC1.D4
  N13: OLED1.SCK, Teensy_LC1.A5/D19
  N14: OLED1.SDA, Teensy_LC1.A4/D18
  N15: Teensy_LC1.D10, S10.1, S10.2
  N16: Teensy_LC1.D12, Teensy_LC1.5Vout
  N17: Teensy_LC1.Program, Teensy_LC1.A12/DAC, Teensy_LC1.D13
  N18: Teensy_LC1.A7/D21, Teensy_LC1.A11

custom parts:
  OLED 128x64 I2C Monochrome Display VDD-GND: OLED 128x64 I2C Monochrome Display. Note: there are two variants of this part, this one is the VDD GND SCK SDA variant. The other is GND VDD SCK SDA. Make sure you select the part that matches your module as using the incorrect part will probably destroy your module! In addition the mounting holes are marked on silkscreen but not by default drilled. If you want drilled mounting holes, copy a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
  Teensy-LC: Teensy-LC (Low Cost) is a powerful 32 bit microcontroller board, with a rich set of hardware peripherals, at a very affordable price! Teensy-LC delivers an impressive collection of capabilities to make modern electronic projects simpler. It features an ARM Cortex-M0+ processor at 48 MHz, 62K Flash, 8K RAM, 12 bit analog input & output, hardware Serial, SPI & I2C, USB, and a total of 27 I/O pins.
