# Fritzing sketch aciduino_v2-avr_mega (saved by Fritzing 0.9.3b)
breadboards: 1

parts:
  S2 = Momentary Switch [package=ksa_sealed_tac_switch]
  S4 = Momentary Switch [package=ksa_sealed_tac_switch]
  S1 = Momentary Switch [package=ksa_sealed_tac_switch]
  S3 = Momentary Switch [package=ksa_sealed_tac_switch]
  S7 = Momentary Switch [package=ksa_sealed_tac_switch]
  S5 = Momentary Switch [package=ksa_sealed_tac_switch]
  S6 = Momentary Switch [package=ksa_sealed_tac_switch]
  S8 = Momentary Switch [package=ksa_sealed_tac_switch]
  R1 = Rotary Potentiometer (Small) [maximum_resistance=100kΩ package=THT]
  S9 = Momentary Switch [package=ksa_sealed_tac_switch]
  OLED1 = OLED 128x64 I2C Monochrome Display VDD-GND
  Part1 = Arduino Mega ADK (Rev3)
  S10 = Momentary Switch [package=ksa_sealed_tac_switch]

nets:
  N1: S2.2, Part1.D5_PWM
  GND: S2.4, S4.1, S4.2, S1.1, S3.3, S3.4, S7.3, S7.4, S5.3, S5.4, S6.1, S6.2, S8.1, S8.2, R1.leg2, S9.3, S9.4, OLED1.GND, Part1.GND, Part1.D11_PWM, S10.3, S10.4
  N2: S4.3, S4.4, Part1.D3_PWM
  N3: S1.3, Part1.D2_PWM
  N4: S3.1, S3.2, Part1.D4_PWM
  N5: S7.1, S7.2, Part1.D10_PWM
  N6: S5.1, S5.2, Part1.D12_PWM
  N7: S6.3, S6.4
  N8: S8.3, S8.4, Part1.D6_PWM
  VDD: R1.leg1, OLED1.VDD, Part1.5V
  N9: R1.wiper, Part1.A8
  N10: S9.1, S9.2, Part1.D13_PWM
  N11: OLED1.SCK, Part1.D21/SCL
  N12: OLED1.SDA, Part1.D20/SDA
  N13: Part1.D7_PWM, S10.1, S10.2

custom parts:
  OLED 128x64 I2C Monochrome Display VDD-GND: OLED 128x64 I2C Monochrome Display. Note: there are two variants of this part, this one is the VDD GND SCK SDA variant. The other is GND VDD SCK SDA. Make sure you select the part that matches your module as using the incorrect part will probably destroy your module! In addition the mounting holes are marked on silkscreen but not by default drilled. If you want drilled mounting holes, copy a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
