# Fritzing sketch aciduino_v2-esp32-30pins (saved by Fritzing 1.0.1rc)
breadboards: 1

parts:
  S2 = Momentary Switch [package=ksa_sealed_tac_switch]
  S4 = Momentary Switch [package=ksa_sealed_tac_switch]
  S1 = Momentary Switch [package=ksa_sealed_tac_switch]
  S3 = Momentary Switch [package=ksa_sealed_tac_switch]
  S7 = Momentary Switch [package=ksa_sealed_tac_switch]
  S5 = Momentary Switch [package=ksa_sealed_tac_switch]
  S6 = Momentary Switch [package=ksa_sealed_tac_switch]
  S8 = Momentary Switch [package=ksa_sealed_tac_switch]
  R1 = Rotary Potentiometer (Small) [maximum_resistance=100kΩ knob_status=50% power=0.5W package=THT]
  S9 = Momentary Switch [package=ksa_sealed_tac_switch]
  Squix1 = OLED 0.96" 128x64 I2C SSD1306
  S10 = Momentary Switch [package=ksa_sealed_tac_switch]
  M1 = DOIT Esp32 DevKit v1 (30 pins long, 11 pins width) [part_number=ESP32S-PIN30]

nets:
  N1: S2.2, M1.D5
  GND: S2.4, S4.1, S4.2, S1.1, S3.3, S3.4, S7.3, S7.4, S5.3, S5.4, S6.1, S6.2, S8.1, S8.2, R1.leg2, S9.3, S9.4, Squix1.GND, M1.D27, M1.GND
  N2: S4.3, S4.4, M1.D19
  N3: S1.3, M1.D23
  N4: S3.1, S3.2, M1.D18
  N5: S7.1, S7.2, M1.D33
  N6: S5.1, S5.2, M1.D14
  N7: S6.3, S6.4
  N8: S8.3, S8.4, M1.D32
  VCC: R1.leg1, Squix1.VCC, M1.3V3
  N9: R1.wiper, M1.D15
  N10: S9.1, S9.2, M1.D12
  N11: Squix1.SCL, M1.D22
  N12: Squix1.SCA, M1.D21
  N13: S10.1, S10.2
  N14: S10.3, S10.4

custom parts:
  DOIT Esp32 DevKit v1 (30 pins long, 11 pins width): The DOIT Esp32 DevKit v1 is one of the development board created by DOIT to evaluate the ESP-WROOM-32 module. It is based on the ESP32 microcontroller that boasts Wifi, Bluetooth, Ethernet and Low Power support all in a single chip. (vanepp) made breadboard work, adjusted pin numbering and labels and reduced size of schematic and cleaned up pcb. This chip is 30pins long (2 x15) and 11 pins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
