# Fritzing sketch aciduino_v2-esp32-wroom-30pins-protoboard (saved by Fritzing 1.0.1rc)
breadboards: 1

parts:
  S2 = Momentary Switch [package=ksa_sealed_tac_switch]
  S4 = Momentary Switch [package=ksa_sealed_tac_switch]
  S1 = Momentary Switch [package=ksa_sealed_tac_switch]
  S3 = Momentary Switch [package=ksa_sealed_tac_switch]
  S7 = Momentary Switch [package=ksa_sealed_tac_switch]
  S5 = Momentary Switch [package=ksa_sealed_tac_switch]
  S6 = Momentary Switch [package=ksa_sealed_tac_switch]
  S8 = Momentary Switch [package=ksa_sealed_tac_switch]
  R1 = Rotary Potentiometer (Small) [maximum_resistance=100kΩ knob_status=50% power=0.5W package=THT]  # not connected
  S9 = Momentary Switch [package=ksa_sealed_tac_switch]
  Squix1 = OLED 0.96" 128x64 I2C SSD1306  # not connected
  M1 = DOIT Esp32 DevKit v1 (30 pins long, 11 pins width) [part_number=ESP32S-PIN30]  # not connected
  R2 = Rotary Potentiometer (Small) [maximum_resistance=100kΩ knob_status=50% power=0.5W package=THT]
  R3 = Rotary Potentiometer (Small) [maximum_resistance=100kΩ knob_status=50% power=0.5W package=THT]  # not connected
  R4 = Rotary Potentiometer (Small) [maximum_resistance=100kΩ knob_status=50% power=0.5W package=THT]  # not connected
  RE1 = Rotary Encoder [package=THT]  # not connected
  R5 = Rotary Potentiometer (Small) [maximum_resistance=100kΩ knob_status=50% power=0.5W package=THT]  # not connected
  R6 = Rotary Potentiometer (Small) [maximum_resistance=100kΩ knob_status=50% power=0.5W package=THT]  # not connected
  R7 = Rotary Potentiometer (Small) [maximum_resistance=100kΩ knob_status=50% power=0.5W package=THT]  # not connected
  R8 = Rotary Potentiometer (Small) [maximum_resistance=100kΩ knob_status=50% power=0.5W package=THT]  # not connected
  R9 = Rotary Potentiometer (Small) [maximum_resistance=100kΩ knob_status=50% power=0.5W package=THT]  # not connected
  U1 = MIDI_CONN_FEMALE_SUPPORT [package=din_5_female_support]  # not connected
  U2 = MIDI_CONN_FEMALE_SUPPORT [package=din_5_female_support]  # not connected

nets:
  N1: S2.4, S4.1, S4.2
  N2: S4.3, S4.4
  N3: S1.1, S3.3, S3.4
  N4: S3.1, S3.2
  N5: S7.1, S7.2
  N6: S7.3, S7.4
  N7: S5.1, S5.2
  N8: S5.3, S5.4
  N9: S6.1, S6.2
  N10: S6.3, S6.4
  N11: S8.1, S8.2
  N12: S8.3, S8.4
  N13: S9.4, R2.wiper

custom parts:
  DOIT Esp32 DevKit v1 (30 pins long, 11 pins width): The DOIT Esp32 DevKit v1 is one of the development board created by DOIT to evaluate the ESP-WROOM-32 module. It is based on the ESP32 microcontroller that boasts Wifi, Bluetooth, Ethernet and Low Power support all in a single chip. (vanepp) made breadboard work, adjusted pin numbering and labels and reduced size of schematic and cleaned up pcb. This chip is 30pins long (2 x15) and 11 pins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
