# Fritzing sketch aciduino_v2-esp32 (saved by Fritzing 0.9.3b)
breadboards: 1

parts:
  S2 = Momentary Switch [package=ksa_sealed_tac_switch]
  S4 = Momentary Switch [package=ksa_sealed_tac_switch]
  S1 = Momentary Switch [package=ksa_sealed_tac_switch]
  S3 = Momentary Switch [package=ksa_sealed_tac_switch]
  S7 = Momentary Switch [package=ksa_sealed_tac_switch]
  S5 = Momentary Switch [package=ksa_sealed_tac_switch]
  S6 = Momentary Switch [package=ksa_sealed_tac_switch]
  S8 = Momentary Switch [package=ksa_sealed_tac_switch]
  R1 = Rotary Potentiometer (Small) [maximum_resistance=100kΩ package=THT]
  S9 = Momentary Switch [package=ksa_sealed_tac_switch]
  OLED1 = OLED 128x64 I2C Monochrome Display VDD-GND
  U1 = ESP32-38PinWide [part_number=ESP32-38PinWide]

nets:
  N1: S2.2, U1.GPIO35
  N2: S2.4, S4.1, S4.2, S1.1, S3.3, S3.4, S7.3, S7.4, S5.3, S5.4, S6.1, S6.2, S8.1, S8.2, R1.leg2, S9.3, S9.4, OLED1.GND, U1.GPIO27, U1.GPIO11
  N3: S4.3, S4.4, U1.GPIO39
  N4: S1.3, U1.GPIO36
  N5: S3.1, S3.2, U1.GPIO34
  N6: S7.1, S7.2, U1.GPIO33
  N7: S5.1, S5.2, U1.GPIO14
  N8: S6.3, S6.4
  N9: S8.3, S8.4, U1.GPIO32
  N10: R1.leg1, OLED1.VDD, U1.3.3
  N11: R1.wiper, U1.GPIO0
  N12: S9.1, S9.2, U1.GPIO12
  N13: OLED1.SCK, U1.GPIO22
  N14: OLED1.SDA, U1.GPIO21

custom parts:
  OLED 128x64 I2C Monochrome Display VDD-GND: OLED 128x64 I2C Monochrome Display. Note: there are two variants of this part, this one is the VDD GND SCK SDA variant. The other is GND VDD SCK SDA. Make sure you select the part that matches your module as using the incorrect part will probably destroy your module! In addition the mounting holes are marked on silkscreen but not by default drilled. If you want drilled mounting holes, copy a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
  ESP32-38PinWide: Generic 38-Pin ESP32 with wide format (only access to one side of pins on a breadboard) based on Stephen Lilley's HiLetgo ESP-WROOM-32 ESP32 ESP-32S Development Board.
